# Fritzing sketch Photon Servo interface with Power Switch and Vin Voltage Divider (saved by Fritzing 0.9.3b)
circuit board: 2.85083cm x 4.07875cm
breadboards: 1

parts:
  Photon = Photon
  R82 = Resistor [tolerance=±5% resistance=100k package=THT]
  R84 = Resistor [tolerance=±1% resistance=2.2k package=THT]
  R80 = Resistor [tolerance=±5% resistance=100k package=THT]
  Q80_N-FET = Basic FET N-Channel [package="TO220 [THT]"]
  Q81_P-FET = Basic FET P-Channel [package="TO220 [THT]"]
  R83 = Resistor [tolerance=±1% resistance=4.7k package=THT]
  J1 = Basic Servo
  R85 = Resistor [tolerance=±5% resistance=100k package=THT]
  Q82-N-FET = Basic FET N-Channel [package="TO220 [THT]"]
  J2 = Basic Servo
  S1 = Toggle Switch [package=THT]
  VCC_4_8V = 4 x AAA Battery Mount

nets:
  N1: Photon.A0, R80.Pin_1, Q80_N-FET.gate
  N2: Photon.A1, R84.Pin_1, R83.Pin_0
  N3: Photon.WKP, R85.Pin_1, Q82-N-FET.gate
  N4: Photon.RX, J2.pulse
  N5: Photon.TX, J1.pulse
  N6: Photon.GND, R84.Pin_0, R80.Pin_0, Q80_N-FET.source, R85.Pin_0, Q82-N-FET.source, VCC_4_8V.-
  VCC: Photon.VIN, R82.Pin_1, Q81_P-FET.source, J1.vcc, J2.vcc, S1.L1, S1.COM
  N7: R82.Pin_0, Q80_N-FET.drain, Q81_P-FET.gate
  N8: Q81_P-FET.drain, R83.Pin_1
  GND: J1.gnd, Q82-N-FET.drain, J2.gnd
  N9: S1.L2, VCC_4_8V.+
