# Fritzing sketch Photon Servo interface with Power Switch (saved by Fritzing 0.9.3b)
circuit board: 2.87476cm x 4.0728cm
breadboards: 1

parts:
  Photon = Photon
  J1 = Basic Servo
  J2 = Basic Servo
  R1 = Resistor [tolerance=±5% resistance=100k package=THT]
  Q1 = Basic FET N-Channel [package="TO220 [THT]"]

nets:
  N1: Photon.WKP, R1.Pin_1, Q1.gate
  N2: Photon.RX, J2.pulse
  N3: Photon.TX, J1.pulse
  N4: Photon.GND, R1.Pin_0, Q1.source
  VCC: Photon.VIN, J1.vcc, J2.vcc
  GND: J1.gnd, J2.gnd, Q1.drain
