# Fritzing sketch Photon Servo interface Passive (saved by Fritzing 0.9.3b)
circuit board: 8.46667cm x 5.64444cm
breadboards: 1

parts:
  Photon = Photon
  J1 = Basic Servo
  J2 = Basic Servo

nets:
  N1: Photon.RX, J2.pulse
  N2: Photon.TX, J1.pulse
  GND: Photon.GND, J1.gnd, J2.gnd
  VCC: Photon.VIN, J1.vcc, J2.vcc
