# Fritzing sketch Photon Servo interface with Power Switch and Vin Voltage Divider (saved by Fritzing 0.9.3b)
circuit board: 2.85083cm x 4.07875cm
breadboards: 1

parts:
  Photon = Photon
  R82 = Resistor [tolerance=±5% resistance=100k package=THT]
  R84 = Resistor [tolerance=±1% resistance=2.2k package=THT]
  R80 = Resistor [tolerance=±5% resistance=100k package=THT]
  Q80_N-FET = Basic FET N-Channel [package="TO220 [THT]"]
  Q81_P-FET = Basic FET P-Channel [package="TO220 [THT]"]
  R83 = Resistor [tolerance=±1% resistance=4.7k package=THT]
  J3 = Basic Servo
  R85 = Resistor [tolerance=±5% resistance=100k package=THT]
  Q2 = Basic FET N-Channel [package="TO220 [THT]"]
  J4 = Basic Servo

nets:
  N1: Photon.A0, R80.Pin_1, Q80_N-FET.gate
  N2: Photon.A1, R84.Pin_1, R83.Pin_0
  N3: Photon.WKP, R85.Pin_1, Q2.gate
  N4: Photon.RX, J4.pulse
  N5: Photon.TX, J3.pulse
  N6: Photon.GND, R84.Pin_0, R80.Pin_0, Q80_N-FET.source, R85.Pin_0, Q2.source
  VCC: Photon.VIN, R82.Pin_1, Q81_P-FET.source, J3.vcc, J4.vcc
  N7: R82.Pin_0, Q80_N-FET.drain, Q81_P-FET.gate
  N8: Q81_P-FET.drain, R83.Pin_1
  GND: J3.gnd, Q2.drain, J4.gnd
